# Fritzing sketch color_wheel (saved by Fritzing 0.9.1b)
breadboards: 1

parts:
  LED1 = RGB LED (com. cathode, rgb) [package="5 mm [THT]"]
  R3 = Resistor [tolerance=±5% resistance=330 package=THT]
  D1 = Rectifier Diode [part_number=1N4001 package="300 mil [THT]"]
  R4 = Resistor [tolerance=±5% resistance=100 package=THT]  # not connected
  Part1 = Arduino Nano (Rev3.0)
  R5 = Resistor [tolerance=±5% resistance=330 package=THT]
  R6 = Resistor [tolerance=±5% resistance=330 package=THT]
  VCC1 = Battery

nets:
  N1: LED1.red_anode, R3.Pin_1
  N2: LED1.common_cathode, R6.Pin_1
  N3: LED1.green_anode, Part1.D3, R5.Pin_0
  N4: LED1.blue_anode, R5.Pin_1
  N5: R3.Pin_0, Part1.D6
  N6: D1.cathode, VCC1.+
  N7: D1.anode, Part1.3V3
  N8: Part1.GND, VCC1.-
  N9: Part1.D5, R6.Pin_0

notes:
  6V x 1.5W solar panel will run this circuit until the batteries go bad
  (around 6 months so far) even in winter daylight hours.
  CRITICAL:
  - Battery pack must be 3 AA or 3 AAA H6/NiMH 1.2V rechargeable batteries.

// code stored in the sketch: fritzing_color_wheel.ino
#include <math.h>
#include <SoftwareSerial.h>
#define RED_GROUND 3
#define MAIN_POWER 4
#define GREEN_GROUND 5
#define BLUE_GROUND 6

#define MAX_COLORS 8
#define MAX_COLOR_LOOP 8

#define MAIN_DELAY 8
#define HOLD_DELAY 13
#define FADE_DELAY 23

#define DEBUG_PIN 12

int R = 255;

int G = 255;

int B = 255;


//DEFINE RGB STRUCT
struct rgbColors {
  int R;
  int G;
  int B;
};

//SUMMER
/**
 rgbColors WheelColors[MAX_COLOR_LOOP] = {
   {253,3,3},
   {255,128,4},
   {255,223,4},
   {56,255,4},
   {90,214,245},
   {153,75,213},
   {244,168,247},
   {248,229,140}
 };
 **/

//AUTUMN
rgbColors WheelColors[MAX_COLOR_LOOP] = {
  {153, 20, 10},
  {252, 107, 1},
  {235, 177, 20},
  {0, 103, 27},
  {8, 47, 126},
  {48, 10, 78},
  {136, 56, 143},
  {108, 44, 3}
};

int getColor(int sc, int ec, int incr, int total);

void setRGB(int R, int G, int B);

void colorWheel(void);

void setup() {

  Serial.begin(9600);
  pinMode(DEBUG_PIN, INPUT);
  pinMode(RED_GROUND, OUTPUT);
  pinMode(GREEN_GROUND, OUTPUT);
  pinMode(BLUE_GROUND, OUTPUT);
  pinMode(MAIN_POWER, OUTPUT);

  digitalWrite(DEBUG_PIN, HIGH);
  digitalWrite(MAIN_POWER, HIGH);
  digitalWrite(RED_GROUND, LOW);
  digitalWrite(GREEN_GROUND, LOW);
  digitalWrite(BLUE_GROUND, LOW);
}


void loop() {
  colorWheel();
  delay(MAIN_DELAY);
}

void colorWheel(void) {

  int i;

  int total;

  int next_i;

  int R, G, B;

  int max_range;

  int start;

  for (i = 0; i < MAX_COLOR_LOOP; i++) {

    if ( i < (MAX_COLOR_LOOP - 1) ) {
      next_i = (int)(i + 1);
    } else {
      next_i = 0;
    }

    R = WheelColors[i].R;
    G = WheelColors[i].G;
    B = WheelColors[i].B;

    setRGB(R, G, B);

    max_range = 255;

    start = 0;

    while (true) {
      if ( (R == WheelColors[next_i].R) && (G == WheelColors[next_i].G) && (B ==  WheelColors[next_i].B) ) {
        delay(HOLD_DELAY);
        break;
      }
      start++;

      setRGB(R, G, B);

      R = getColor(R, WheelColors[next_i].R, start, max_range);

      G = getColor(G, WheelColors[next_i].G, start, max_range);

      B = getColor(B, WheelColors[next_i].B, start, max_range);

      setRGB(R, G, B);

      double debug = analogRead(DEBUG_PIN);

      if ((Serial.available()>0) && (debug >= 1.0)) {
        Serial.print("R,G,B");
        Serial.print(R);
        Serial.print(" , ");
        Serial.print(G);
        Serial.print(" , ");
        Serial.print(B);
        Serial.println(" , ");
        Serial.print(start);
        Serial.print(" , ");
      }

      delay(FADE_DELAY);
      if ((start == max_range)) {
        start = -254;
        continue;
      }
    }
  }
}

int getColor(int sc, int ec, int incr, int total) {

  int color = (int)sc + (int)(((ec - sc) * incr) / total);

  return color;
}

void setRGB(int R, int G, int B) {

  analogWrite(RED_GROUND, abs(255 - R) );

  analogWrite(GREEN_GROUND, abs(255 - G) );

  analogWrite(BLUE_GROUND, abs(255 - B) );
}
